# Fritzing sketch balidazio ariketa1 (saved by Fritzing 0.9.3b)
breadboards: 1

parts:
  IC2 = 4011 4 x 2 Input NAND Gate, single part [part_number=4011 package="DIP (Dual Inline) [THT]"]
  S1 = Momentary Switch [package=ksa_sealed_tac_switch]
  R1 = Resistor [tolerance=±5% resistance=220 package=THT]
  VCC1 = 4 x AAA Battery Mount
  S2 = Pushbutton [package="[THT]"]
  R2 = Resistor [tolerance=±5% resistance=220 package=THT]
  S3 = Pushbutton [package="[THT]"]
  R3 = Resistor [tolerance=±5% resistance=220 package=THT]
  IC3 = 4011 4 x 2 Input NAND Gate, single part [part_number=4011 package="DIP (Dual Inline) [THT]"]
  IC4 = 4011 4 x 2 Input NAND Gate, single part [part_number=4011 package="DIP (Dual Inline) [THT]"]
  LED1 = LED - 5mm [color="Red (633nm)" package="5 mm [THT]"]
  LED2 = LED - 5mm [color="Green (570nm)" package="5 mm [THT]"]
  R4 = Resistor [tolerance=±5% resistance=220 package=THT]
  R5 = Resistor [tolerance=±5% resistance=220 package=THT]

nets:
  N1: IC2.A1, IC2.B1, S1.4, R1.Pin_0
  N2: IC2.Q1, IC2.B2, IC4.A4
  N3: IC2.Q2, IC2.A3, IC2.B3
  N4: IC2.A2, S2.Pin_3, S2.Pin_4, R2.Pin_0, IC3.A4
  GND: IC2.GND, R1.Pin_1, VCC1.-, R2.Pin_1, R3.Pin_1, IC3.GND, IC4.GND, R4.Pin_1, R5.Pin_1
  N5: IC2.Q3, IC3.B1
  N6: IC2.Q4, IC3.A1
  N7: IC2.A4, IC2.B4, S3.Pin_3, S3.Pin_4, R3.Pin_0, IC3.B4
  VDD: IC2.VDD, S1.1, VCC1.+, S2.Pin_1, S2.Pin_2, S3.Pin_1, S3.Pin_2, IC3.VDD, IC4.VDD
  N8: IC3.Q1, IC3.A2, IC3.B2, IC4.B1
  N9: IC3.Q2, LED1.anode
  N10: IC3.A3, IC3.B3, IC3.Q4
  N11: IC3.Q3, IC4.B4
  N12: IC4.A1, IC4.Q3
  N13: IC4.Q1, IC4.A2, IC4.B2
  N14: IC4.Q2, LED2.anode
  N15: IC4.A3, IC4.B3, IC4.Q4
  N16: LED1.cathode, R4.Pin_0
  N17: LED2.cathode, R5.Pin_0
