# Fritzing sketch balidazio ariketa2 (saved by Fritzing 0.9.3b)
breadboards: 1

parts:
  Part1 = iceZUM Alhambra
  SW1 = DIP Switch 8 Position [package=dipswitch-08]
  R1 = Resistor [tolerance=±5% resistance=220 package=THT]
  R2 = Resistor [tolerance=±5% resistance=220 package=THT]
  R3 = Resistor [tolerance=±5% resistance=220 package=THT]
  R4 = Resistor [tolerance=±5% resistance=220 package=THT]
  R5 = Resistor [tolerance=±5% resistance=220 package=THT]
  LED1 = LED - 5mm [color="Red (633nm)" package="5 mm [THT]"]
  LED2 = LED - 5mm [color="Green (570nm)" package="5 mm [THT]"]
  J1 = Power Jack [package=power_jack_combo]
  VCC1 = Battery block 9V

nets:
  N1: Part1.D1, SW1.16, R1.Pin_0
  N2: Part1.D2, SW1.15, R2.Pin_0
  N3: Part1.D3, SW1.14, R3.Pin_0
  N4: Part1.D5, R5.Pin_1
  N5: Part1.D6, R4.Pin_1
  N6: Part1.GD2, Part1.GND, R1.Pin_1, R2.Pin_1, R3.Pin_1, LED1.anode, LED2.anode
  N7: Part1.5V, SW1.1, SW1.2, SW1.3
  N8: R4.Pin_0, LED2.cathode
  N9: R5.Pin_0, LED1.cathode
  N10: J1.GND, VCC1.+
  N11: J1.GNDBREAK, VCC1.-

notes:
  ICEZUM JACK
  Diodoak alderantziz polarizatu dituzu!!
  Gainontzekoa bikain!!

custom parts:
  iceZUM Alhambra: Arduino/zum compatible Open FPGA electronic board. Synthesize hardware easily, using only open source tools
