# Fritzing sketch balidazio ariketa3 (saved by Fritzing 0.9.3b)
breadboards: 1

parts:
  IC1 = L293D [package=THT]
  M1 = DC Motor
  Part1 = iceZUM Alhambra
  VCC1 = Battery block 9V

nets:
  N1: IC1.Enable_1, Part1.D10
  N2: IC1.In_1, Part1.D8
  N3: IC1.0V, Part1.GD4, Part1.GND, VCC1.-
  N4: IC1.In_2, Part1.D9
  N5: IC1.Out_3_(_Controlled_by_Enable_2_), M1.pin_2
  N6: IC1.Out_4_(_Controlled_by_Enable_2_), M1.pin_1
  N7: IC1.+V, VCC1.+

notes:
  El L293 tiene dos puentes en H. Has llevado las entradas a una y has conectado el motor al otro.
  El L293 se alimenta a V por el pin 16, y no a 9V!!
  El puente en H alimenta el motor con tensión de bateria del pin 8, que esta sin conectar

custom parts:
  iceZUM Alhambra: Arduino/zum compatible Open FPGA electronic board. Synthesize hardware easily, using only open source tools
