# Fritzing sketch Ariketa 3 Armando (saved by Fritzing 0.9.3b)
breadboards: 1

parts:
  Componente1 = iceZUM Alhambra
  IC1 = L293D [package=THT]
  VCC1 = Battery block 9V  # not connected
  J2 = Power Jack [package=power_jack_smd]  # not connected

nets:
  N1: Componente1.GND, IC1.0V

custom parts:
  iceZUM Alhambra: Arduino/zum compatible Open FPGA electronic board. Synthesize hardware easily, using only open source tools
