# Fritzing sketch balidazio ariketa3 (saved by Fritzing 0.9.3b)
breadboards: 1

parts:
  IC1 = L293D [package=THT]
  M1 = DC Motor
  Part1 = iceZUM Alhambra
  VCC1 = Battery block 9V

nets:
  N1: IC1.Enable_1, Part1.D3, Part1.V3
  N2: IC1.In_1, Part1.D1, Part1.V1
  N3: IC1.Out_1_(_Controlled_by_Enable_1_), M1.pin_1
  N4: IC1.0V, VCC1.-
  N5: IC1.Out_2_(_Controlled_by_Enable_1_), M1.pin_2
  N6: IC1.In_2, Part1.D2, Part1.V2
  N7: IC1.+V, VCC1.+

notes:
  ICEZUM-a elikatzea fala da.
  L293 ez da bateriatik elikatu behar 5V-kin baizik.
  L293-ko 8. pin-ean bateriako tentsioa sartu behar da motorra elikatzeko

custom parts:
  iceZUM Alhambra: Arduino/zum compatible Open FPGA electronic board. Synthesize hardware easily, using only open source tools
