# Fritzing sketch balidazio ariketa2 (saved by Fritzing 0.9.3b)
breadboards: 1

parts:
  Part1 = iceZUM Alhambra
  SW1 = DIP Switch 8 Position [package=dipswitch-08]  # not connected
  R1 = Resistor [tolerance=±5% resistance=220 package=THT]
  R2 = Resistor [tolerance=±5% resistance=220 package=THT]
  R3 = Resistor [tolerance=±5% resistance=220 package=THT]
  R4 = Resistor [tolerance=±5% resistance=220 package=THT]
  R5 = Resistor [tolerance=±5% resistance=220 package=THT]
  LED1 = LED - 5mm [color="Red (633nm)" package="5 mm [THT]"]
  LED2 = LED - 5mm [color="Green (570nm)" package="5 mm [THT]"]
  VCC1 = Battery block 9V

nets:
  N1: Part1.D0, R3.Pin_0
  N2: Part1.D1, R2.Pin_0
  N3: Part1.D2, R1.Pin_0
  N4: Part1.D3, R4.Pin_1
  N5: Part1.D4, R5.Pin_1
  N6: R1.Pin_1, R2.Pin_1, R3.Pin_1, LED1.cathode, LED2.cathode, VCC1.-
  N7: R4.Pin_0, LED1.anode
  N8: R5.Pin_0, LED2.anode

notes:
  9V sartu dituzu ICEZUM-eko sarreretan. Hori ezin da egin
  Ez duzu ICEZUM-a elikatu!
  Sarrerako pull-down-ak eta diodoen konekzioa ondo.

custom parts:
  iceZUM Alhambra: Arduino/zum compatible Open FPGA electronic board. Synthesize hardware easily, using only open source tools
