# Fritzing sketch Nahuel (saved by Fritzing 0.9.3b)
breadboards: 1

parts:
  Part1 = iceZUM Alhambra
  SW1 = DIP Switch 8 Position [package=dipswitch-08]
  R1 = Resistor [tolerance=±5% resistance=1k package=THT]
  R2 = Resistor [tolerance=±5% resistance=1k package=THT]
  R3 = Resistor [tolerance=±5% resistance=1k package=THT]
  R4 = Resistor [tolerance=±5% resistance=220 package=THT]
  R5 = Resistor [tolerance=±5% resistance=220 package=THT]
  LED1 = LED - 5mm [color="Red (633nm)" package="5 mm [THT]"]
  LED2 = LED - 5mm [color="Green (570nm)" package="5 mm [THT]"]
  VCC1 = Battery block 9V

nets:
  N1: Part1.D2, Part1.V2, LED2.anode
  N2: Part1.D3, LED1.anode
  N3: Part1.D11, SW1.8, R3.Pin_0
  N4: Part1.D12, SW1.4, R2.Pin_0
  N5: Part1.D13, SW1.1, R1.Pin_0
  N6: Part1.GD2, Part1.GND, R2.Pin_1, R3.Pin_1, R4.Pin_1, R5.Pin_1, VCC1.-
  N7: Part1.VIN, SW1.9, SW1.13, SW1.16, VCC1.+
  N8: R4.Pin_0, LED1.cathode
  N9: R5.Pin_0, LED2.cathode

notes:
  9V sartu dituzu ICEZUM-eko sarrera digitaletan!!
  5V bakarrik onartzen dira.

custom parts:
  iceZUM Alhambra: Arduino/zum compatible Open FPGA electronic board. Synthesize hardware easily, using only open source tools
