# Fritzing sketch Ariketa 3 Nahuel (saved by Fritzing 0.9.3b)
breadboards: 1

parts:
  IC1 = L293D [package=THT]
  M1 = DC Motor
  Part1 = iceZUM Alhambra
  VCC1 = Battery block 9V

nets:
  N1: IC1.Enable_1, Part1.5V
  N2: IC1.In_1, Part1.D9
  N3: IC1.Out_1_(_Controlled_by_Enable_1_), M1.pin_2
  N4: IC1.0V, IC1.Out_2_(_Controlled_by_Enable_1_), IC1.+V, Part1.D8, Part1.GND, VCC1.-
  N5: IC1.In_2, M1.pin_1
  N6: IC1.+Vmotor, Part1.VIN, VCC1.+

notes:
  L293-ko 4, 6 eta 7 hankak ez daude ondo.

custom parts:
  iceZUM Alhambra: Arduino/zum compatible Open FPGA electronic board. Synthesize hardware easily, using only open source tools
