# Fritzing sketch balidazio ariketa2 Ronny (saved by Fritzing 0.9.3b)
breadboards: 1

parts:
  Part1 = iceZUM Alhambra
  SW1 = DIP Switch 8 Position [package=dipswitch-08]
  R1 = Resistor [tolerance=±5% resistance=220 package=THT]
  R2 = Resistor [tolerance=±5% resistance=220 package=THT]
  R3 = Resistor [tolerance=±5% resistance=220 package=THT]
  R4 = Resistor [tolerance=±5% resistance=220 package=THT]
  R5 = Resistor [tolerance=±5% resistance=220 package=THT]
  LED1 = LED - 5mm [color="Red (633nm)" package="5 mm [THT]"]
  LED2 = LED - 5mm [color="Green (570nm)" package="5 mm [THT]"]
  VCC1 = Battery block 9V

nets:
  N1: Part1.D1, Part1.V1, LED2.anode
  N2: Part1.D2, LED1.anode
  N3: Part1.D8, Part1.V8, SW1.1, R1.Pin_0
  N4: Part1.D9, SW1.3, R2.Pin_0
  N5: Part1.D10, SW1.5, R3.Pin_0
  N6: Part1.5V, SW1.12, SW1.14, SW1.16
  N7: Part1.GND, R1.Pin_1, R2.Pin_1, R3.Pin_1, R4.Pin_1, R5.Pin_1, VCC1.-
  N8: Part1.VIN, VCC1.+
  N9: R4.Pin_0, LED1.cathode
  N10: R5.Pin_0, LED2.cathode

notes:
  Oso ondo!

custom parts:
  iceZUM Alhambra: Arduino/zum compatible Open FPGA electronic board. Synthesize hardware easily, using only open source tools
