# Fritzing sketch balidazio ariketa3 (saved by Fritzing 0.9.3b)
breadboards: 1

parts:
  IC1 = L293D [package=THT]
  M1 = DC Motor
  Part1 = iceZUM Alhambra
  VCC1 = Battery block 9V

nets:
  N1: IC1.In_1, Part1.D13
  N2: IC1.Out_1_(_Controlled_by_Enable_1_), M1.pin_1
  N3: IC1.0V, Part1.GD1, Part1.GND, VCC1.-
  N4: IC1.Out_2_(_Controlled_by_Enable_1_), M1.pin_2
  N5: IC1.In_2, Part1.D12
  N6: IC1.+Vmotor, IC1.+V, Part1.5V
  N7: Part1.VIN, VCC1.+

notes:
  Driver-eko Vmotor-en 5V sartu dituzu, bateriako 9V sartu behar zirenean.

custom parts:
  iceZUM Alhambra: Arduino/zum compatible Open FPGA electronic board. Synthesize hardware easily, using only open source tools
