# Fritzing sketch balidazio ariketa3 (saved by Fritzing 0.9.3b)
breadboards: 1

parts:
  IC1 = L293D [package=THT]
  M1 = DC Motor
  Part1 = iceZUM Alhambra
  VCC1 = Battery block 9V

nets:
  N1: IC1.Enable_1, IC1.+Vmotor, IC1.Enable_2, Part1.V11
  N2: IC1.In_1, Part1.SCL
  N3: IC1.Out_1_(_Controlled_by_Enable_1_), M1.pin_2
  N4: IC1.0V, Part1.G9, VCC1.-
  N5: IC1.Out_2_(_Controlled_by_Enable_1_), M1.pin_1
  N6: IC1.In_2, Part1.SDA
  N7: IC1.+V, VCC1.+

notes:
  Los pines 8 y 16 estan invertidos. Por el 8 se conecta la tension de bateria para alimentar los motores. Y por el 16 se alimenta el chip a 5V.
  La ICEZUM no esta alimentada
  Los pines de salida del ICEZUM no son los correctos.

custom parts:
  iceZUM Alhambra: Arduino/zum compatible Open FPGA electronic board. Synthesize hardware easily, using only open source tools
